# Fritzing sketch Untitled Sketch (saved by Fritzing 0.9.3b)
breadboards: 1

parts:
  元件1 = Arduino Ethernet Shield (Rev3)
  D1 = LED_BARGRAPH_10 [package=led_bargaph_10]
  R1 = Resistor [tolerance=±5% resistance=220 package=THT]
  R2 = Resistor [tolerance=±5% resistance=220 package=THT]
  R3 = Resistor [tolerance=±5% resistance=220 package=THT]
  R4 = Resistor [tolerance=±5% resistance=220 package=THT]
  R5 = Resistor [tolerance=±5% resistance=220 package=THT]
  R7 = Resistor [tolerance=±5% resistance=220 package=THT]
  R8 = Resistor [tolerance=±5% resistance=220 package=THT]
  R9 = Resistor [tolerance=±5% resistance=220 package=THT]
  R10 = Resistor [tolerance=±5% resistance=220 package=THT]
  R11 = Resistor [tolerance=±5% resistance=220 package=THT]
  J1 = Basic Force Sensing Resistor (FSR) [package=THT]
  R12 = Resistor [tolerance=±5% resistance=220 package=THT]
  元件2 = OLED Monochrome 128x64 0.96 inch [part_number=326]

nets:
  N1: 元件1.D8, 元件2.GND
  N2: 元件1.PWM_D9, 元件2.RESET
  N3: 元件1.ETH_CS, 元件2.VIN
  N4: 元件1.PWM_D11, 元件2.3.3V
  N5: 元件1.SPI/D12, 元件2.CS
  N6: 元件1.GND, R1.Pin_0, R2.Pin_0, R3.Pin_0, R4.Pin_0, R5.Pin_0, R7.Pin_0, R8.Pin_0, R9.Pin_0, R10.Pin_0, R11.Pin_0, 元件2.SCLK_SCK
  N7: 元件1.A0, J1.pin_1
  N8: 元件1.D2, D1.J_C
  N9: 元件1.PWM_D3, D1.I_C
  N10: 元件1.SDCS, D1.H_C
  N11: 元件1.PWM_D5, D1.G_C
  N12: 元件1.PWM_D6, D1.F_C
  N13: 元件1.D7, D1.E_C
  N14: 元件1.5V, J1.pin_0, R12.Pin_1, 元件2.DC_SA0
  N15: D1.A_A, R7.Pin_1
  N16: D1.B_A, R8.Pin_1
  N17: D1.C_A, R9.Pin_1
  N18: D1.D_A, R10.Pin_1
  N19: D1.E_A, R11.Pin_1
  N20: D1.F_A, R5.Pin_1
  N21: D1.G_A, R4.Pin_1
  N22: D1.H_A, R3.Pin_1
  N23: D1.I_A, R2.Pin_1
  N24: D1.J_A, R1.Pin_1

custom parts:
  OLED Monochrome 128x64 0.96 inch: These displays are small, only about 1" diameter, but very readable due to the high contrast of an OLED display. This display is made of 128x64 individual white OLED pixels, each one is turned on or off by the controller chip. Because the display makes its own light, no backlight is required. This reduces the power required to run the OLED and is why the display has such high contrast; we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
